# Fritzing sketch newest_electronic_sketch_lcd_wemos (saved by Fritzing 1.0.4)
breadboards: 1

parts:
  Composant1 = Arduino Uno (Rev3) - ICSP  # not connected
  LCD1 = LCD screen
  IC1 = SELECTOR_MULTIPLEXER [package=so016]  # not connected
  M3 = RioRand LM2596
  Composant2 = InvenSense MPU6050  # not connected
  M5 = Stepper Motor - Bipolar
  RE1 = Rotary Encoder [package=THT]  # not connected
  Arduino_CNC_Shield_V3_00_1 = Arduino_CNC_V3.00
  Power_plug2 = Power plug
  JL012-13-5_1 = JL012-13-5.2 Lever (Limit) Switch SPDT + NO + NC [part_number=JL012-13-5.2]
  JL012-13-5_2 = JL012-13-5.2 Lever (Limit) Switch SPDT + NO + NC [part_number=JL012-13-5.2]
  J1 = Basic Servo
  M8 = Dagu DGServo 9g (Top view) [part_number=RS001B]
  M9 = Dagu DGServo 9g (Top view) [part_number=RS001B]
  M10 = >Wemos D1 R32

nets:
  GND: LCD1.VSS, LCD1.LED-, M3.Pin_4, J1.gnd, M8.gnd, M9.gnd, M10.GND
  VDD: LCD1.VDD, M10.3V3
  N1: LCD1.RS, M10.IO18
  N2: LCD1.E, M10.IO19
  N3: LCD1.DB4, M10.IO16
  N4: LCD1.DB5, M10.IO17
  N5: LCD1.DB6, M10.IO25
  N6: LCD1.DB7, M10.IO26
  N7: LCD1.LED+, M10.5V
  N8: M3.Pin_1, Power_plug2.VCC
  N9: M3.Pin_2, Power_plug2.GND
  VCC: M3.Pin_3, J1.vcc, M9.vcc, M10.VN
  N10: M5.A, Arduino_CNC_Shield_V3_00_1.Z-MTR_'4'
  N11: M5.C, Arduino_CNC_Shield_V3_00_1.Z-MTR_'3'
  N12: M5.B, Arduino_CNC_Shield_V3_00_1.Z-MTR_'2'
  N13: M5.D, Arduino_CNC_Shield_V3_00_1.Z-MTR_'1'
  N14: Arduino_CNC_Shield_V3_00_1.RX, M10.RX0
  N15: Arduino_CNC_Shield_V3_00_1.TX, M10.TX0
  N16: Arduino_CNC_Shield_V3_00_1.SpnEn_/_Z_Limit, JL012-13-5_1.C
  N17: Arduino_CNC_Shield_V3_00_1.SpnEn_(Gnd), JL012-13-5_1.NC
  N18: Arduino_CNC_Shield_V3_00_1.SpnDir, JL012-13-5_2.C
  N19: Arduino_CNC_Shield_V3_00_1.SpnDir_(Gnd), JL012-13-5_2.NC

custom parts:
  Arduino_CNC_V3.00: Protoneer Arduino CNC Shield V3.00 If using Grbl V0.9: The “A” axis can not be used (yet). The “SCL” (Arduino A5) pin is now used for 'Probing' input. The “End Stops Z+ & Z-” (Arduino D11) and “SpnEn” (Arduino D12) have been switched!
  JL012-13-5.2 Lever (Limit) Switch SPDT + NO + NC: Micro Switch; Model No.: JL012-13.5-2; Actuator Action: Momentary; Actuator Type: Hinge Lever; Contact Configuration: 1NO, 1NC (SPDT) Temperature -25~65℃；Relative humidity: below 85%; Rate Voltage: 125V AC; Rated Current: 1A.
  >Wemos D1 R32: Wemos D1 R32 - This board is used with dual-mode Wi-Fi and Bluetooth chips, which is safe, reliable, and scalable to a variety of applications. DC in 5V-12V, 1 analog input(3.2V max input), a Micro USB connection, Compatible with D1 R32=WiFi+bluetooth+UNO
